# Fritzing sketch fritzing_controller_schematic (saved by Fritzing 1.0.5)

parts:
  A1 = ESP32 DevKitc V4
  U1 = POT [knob_status=50% power=0.5W package=pot_mammoth]
  U2 = POT [knob_status=50% power=0.5W package=pot_mammoth]
  U3 = POT [knob_status=50% power=0.5W package=pot_mammoth]
  U4 = POT [knob_status=50% power=0.5W package=pot_mammoth]
  S1 = Momentary Switch [package=ksa_sealed_tac_switch]
  S2 = Toggle Switch [package=THT]
  BATT1 = 3xAAA Switchable Battery Pack w/JST connector

nets:
  N1: A1.Pin_1, U1.S, U2.S, U3.S, U4.S, S2.COM
  N2: A1.Pin_5, U4.A
  N3: A1.Pin_6, U1.A
  N4: A1.Pin_7, U2.A
  N5: A1.Pin_8, U3.A
  N6: A1.Pin_9, S1.3
  N7: A1.Pin_14, A1.Pin_38, U1.E, U2.E, U3.E, U4.E, S1.2, BATT1.NEG
  N8: S2.L1, BATT1.POS

notes:
  2xAA
  Parallel Connections
  ADC Pins

custom parts:
  ESP32 DevKitc V4: ESP32-DevKitC board with ESP32-WROOM-32 module. ESP32-DevKitC V4 is a small-sized ESP32-based development board produced by Espressif. Most of the pins on the ESP module are broken out to the pin headers on the board. The pins D0, D1, D2, D3, CMD and CLK are used internally for communication between ESP32 and SPI flash memory. They are grouped on both sides near the USB connector. Avoid using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
  3xAAA Switchable Battery Pack w/JST connector: 3xAAA Switchable Battery Pack with JST connector
