# Fritzing sketch fritzing_robot_arm_schematic (saved by Fritzing 1.0.5)

parts:
  Part1 = 16-Channel 12-bit PWM Servo Driver - I2C [part_number=815]
  S1 = Toggle Switch [package=THT]
  JACK1 = 2.1mm Barrel Jack with Terminal Block
  A2 = ESP32 DevKitc V4
  M2 = RioRand LM2596
  J2 = Basic Servo
  J3 = Basic Servo
  J4 = Basic Servo
  J5 = Basic Servo
  J6 = Basic Servo

nets:
  N1: Part1.PWRIN, S1.COM, M2.Pin_1
  GND: Part1.GND, JACK1.NEG, A2.Pin_14, A2.Pin_32, A2.Pin_38, M2.Pin_2, M2.Pin_4, J2.gnd, J3.gnd, J4.gnd, J5.gnd, J6.gnd
  N2: Part1.PWM4, J6.pulse
  VCC: Part1.5.0V, J2.vcc, J3.vcc, J4.vcc, J5.vcc, J6.vcc
  N3: Part1.PWM3, J5.pulse
  N4: Part1.PWM2, J4.pulse
  N5: Part1.PWM1, J3.pulse
  N6: Part1.PWM0, J2.pulse
  N7: Part1.VCC, A2.Pin_1
  N8: Part1.SDA, A2.Pin_33
  N9: Part1.SCL, A2.Pin_36
  N10: S1.L1, JACK1.POS
  N11: A2.Pin_4, M2.Pin_3

notes:
  SCL = GPIO22
  SDA = GPIO 21
  Regulate to 3.3 or 5 Volts
  Name each servo

custom parts:
  16-Channel 12-bit PWM Servo Driver - I2C: You want to make a cool robot, maybe a hexapod walker, or maybe just a piece of art with a lot of moving parts. Or maybe you want to drive a lot of LEDs with precise PWM output. Using only two pins, control 16 free-running PWM outputs! You can even chain up 62 breakouts to control up to 992 PWM outputs.
  ESP32 DevKitc V4: ESP32-DevKitC board with ESP32-WROOM-32 module. ESP32-DevKitC V4 is a small-sized ESP32-based development board produced by Espressif. Most of the pins on the ESP module are broken out to the pin headers on the board. The pins D0, D1, D2, D3, CMD and CLK are used internally for communication between ESP32 and SPI flash memory. They are grouped on both sides near the USB connector. Avoid using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
