# Fritzing sketch fritzing_servo_testing_schematic (saved by Fritzing 1.0.5)

parts:
  Part1 = 16-Channel 12-bit PWM Servo Driver - I2C [part_number=815]
  A1 = ESP32 DevKitc V4
  J1 = Basic Servo
  M1 = RioRand LM2596
  JACK1 = 2.1mm Barrel Jack with Terminal Block
  S1 = Toggle Switch [package=THT]

nets:
  N1: Part1.PWRIN, M1.Pin_1, S1.COM
  GND: Part1.GND, A1.Pin_14, A1.Pin_38, J1.gnd, M1.Pin_2, M1.Pin_4, JACK1.NEG
  N2: Part1.PWM0, J1.pulse
  N3: Part1.5.0V, J1.vcc
  N4: Part1.VCC, A1.Pin_1
  N5: Part1.SDA, A1.Pin_33
  N6: Part1.SCL, A1.Pin_36
  N7: A1.Pin_4, M1.Pin_3
  N8: JACK1.POS, S1.L1

notes:
  SDA = 21
  SCL = 22
  Regulate to 3.3V or 5V

custom parts:
  16-Channel 12-bit PWM Servo Driver - I2C: You want to make a cool robot, maybe a hexapod walker, or maybe just a piece of art with a lot of moving parts. Or maybe you want to drive a lot of LEDs with precise PWM output. Using only two pins, control 16 free-running PWM outputs! You can even chain up 62 breakouts to control up to 992 PWM outputs.
  ESP32 DevKitc V4: ESP32-DevKitC board with ESP32-WROOM-32 module. ESP32-DevKitC V4 is a small-sized ESP32-based development board produced by Espressif. Most of the pins on the ESP module are broken out to the pin headers on the board. The pins D0, D1, D2, D3, CMD and CLK are used internally for communication between ESP32 and SPI flash memory. They are grouped on both sides near the USB connector. Avoid using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
